# Fritzing sketch SwitchUSB (saved by Fritzing 0.9.3b)
breadboards: 1

parts:
  USB_In = USB Connectors [package=usb-a-s]
  USB_Out_2 = USB Connectors [package=usb-a-h]
  USB_Out_1 = USB Connectors [package=usb-a-h]
  U3 = RELAY [package=relay-t9a]
  U1 = RELAY [package=relay-t9a]
  S1 = Round Pushbutton

nets:
  N1: USB_In.D+, USB_Out_2.D+
  N2: USB_In.D-, U3.MAIN
  GND: USB_In.GND, USB_Out_2.GND, USB_Out_1.GND, U3.COIL1, U1.COIL2
  N3: USB_In.VBUS, U1.MAIN
  N4: USB_Out_2.D-, U3.NO
  N5: USB_Out_2.VBUS, U1.NC
  N6: USB_Out_1.D-, U3.NC
  N7: USB_Out_1.D+, S1.leg1
  N8: USB_Out_1.VBUS, U1.NO
  N9: U3.COIL2, U1.COIL1, S1.leg0
